// Logisim project RSC.circ as structural Verilog: 17 circuits, main circuit main
module main (
  input  NotFlushSEL,
  input  PC_XM_30,
  input  RESET_PC_BIOS,
  input  PC_FD_30,
  input  REST_PC_BIO,
  input  NOP_FLUSHING
);

  wire AFrwd1, AFrwd2, ALUSel, and_1_out, ASel, BFrwd1, BFrwd2, bios_1_p4, BrSel, BrTaken, BSel, CSRWen,
       dmem_1_p4, DoNotBranch, Flush, JalrFrwd, load_1_p3, load_2_p3, MemRW, multiplexer_2_p6,
       multiplexer_3_out, not_1_out, PCSel, ready_to_receive, reg_1_p6, reg_1_p7, RegWE, store_1_p4,
       store_1_p5, store_1_p6, store_2_p4, store_2_p5, store_2_p6, uart_read_1_p2, undriven, write_valid;
  wire [1:0] uart_write_1_p3;
  wire [3:0] WBSel;
  wire [4:0] reg_1_p2;
  wire [7:0] multiplexer_6_out;
  wire [13:0] adder_1_out, adder_2_out, adder_3_out, adder_4_out, adder_5_out, adder_6_out, adder_7_out,
       adder_8_out, adder_9_out, correct_branch_counter_q, cycle_counter_q, Inst_counter_q, is_branch_instr,
       is_prediction_correct, multiplexer_1_out, multiplexer_4_out, PC_FD_q, PC_W_q, total_branch_counter_q;
  wire [13:1] undriven_2;
  wire [31:0] A_q, ALU_RESULT_W_q, B_q, bios_1_p3, br_pred_taken, br_pred_taken_xm_q, flush_w_q,
       imem_1_b_dout, Imm_q, immediate_1_imm, ImmSel, Inst_W_q, Inst_XM_q, multiplexer_5_out,
       multiplexer_7_out, multiplexer_8_out, multiplexer_10_out, multiplexer_11_out, multiplexer_12_out,
       PC_XM_q, reg_1_p1, store_1_p1, store_1_p2, xm_logic_1_p3;

  Adder #(.width(14)) adder_1 (.a(14'h4), .b(PC_FD_q), .out(adder_1_out));  // open: cin, cout
  Adder #(.width(14)) adder_2 (.a(PC_FD_q), .b(immediate_1_imm[13:0]), .out(adder_2_out));  // open: cin, cout
  Multiplexer multiplexer_1 (
    .in0(multiplexer_6_out[0]), .in1(store_1_p1[0]), .out(multiplexer_1_out[0]), .sel(JalrFrwd));
  Adder #(.width(14)) adder_3 (.a(immediate_1_imm[13:0]), .b(multiplexer_1_out), .out(adder_3_out));  // open: cin, cout
  // Multiplexer #(.select(2), .width(14)) multiplexer_2: pin names not known; wires that end beside it: adder_1_out, adder_3_out, adder_2_out, RESET_PC_BIOS, PCSel, multiplexer_2_p6
  Multiplexer multiplexer_3 (.in0(store_1_p1[0]), .in1(adder_4_out[0]), .out(multiplexer_3_out), .sel(DoNotBranch));
  Multiplexer multiplexer_4 (
    .in0(multiplexer_2_p6), .in1(multiplexer_3_out), .out(multiplexer_4_out[0]), .sel(and_1_out));
  and and_1 (and_1_out, Flush, not_1_out);
  not not_1 (not_1_out, undriven);
  Register #(.width(14)) PC_FD (.D(multiplexer_4_out), .Q(PC_FD_q));  // open: en, clk, clr
  // store store_1: pin names not known; wires that end beside it: store_1_p1, store_1_p2, PC_XM_30, store_1_p4, store_1_p5, store_1_p6
  IMEM imem_1 (
    .A_wbe(store_1_p5), .A_din(store_1_p4), .A_addr(store_1_p6), .B_addr(multiplexer_4_out[0]),
    .B_dout(imem_1_b_dout));  // open: clk
  // BIOS bios_1: pin names not known; wires that end beside it: multiplexer_4_out, store_1_p1, bios_1_p3, bios_1_p4
  Multiplexer #(.width(32)) multiplexer_5 (
    .in0(imem_1_b_dout), .in1(bios_1_p3), .out(multiplexer_5_out), .sel(PC_FD_30));
  Register #(.width(32)) CSR_51E (.D(ALU_RESULT_W_q), .en(CSRWen));  // open: clk, Q, clr
  FD_logic fd_logic_1 ();  // open: InstFd, PCFd, InstSel, ImmSell
  Branch_Pred_logic branch_pred_logic_1 (
    .br_result(BrTaken), .br_pred_taken(br_pred_taken[0]));  // open: PC_FD, is_branch_fd, PC_XM, is_branch_xm
  // Reg reg_1: pin names not known; wires that end beside it: reg_1_p1, reg_1_p2, multiplexer_5_out[19:15], multiplexer_5_out[31:20], RegWE, reg_1_p6, reg_1_p7
  immediate immediate_1 (.Instruc(multiplexer_5_out), .ImmSel(ImmSel), .Imm(immediate_1_imm));
  Register PC_XM (.D(PC_FD_q[7:0]), .Q(PC_XM_q[7:0]));  // open: en, clk, clr
  Register A (.D(multiplexer_6_out), .Q(A_q[7:0]));  // open: en, clk, clr
  Multiplexer multiplexer_6 (.in0(reg_1_p6), .in1(reg_1_p1[0]), .out(multiplexer_6_out[0]), .sel(AFrwd2));
  Register #(.width(32)) B (.D(multiplexer_7_out), .Q(B_q));  // open: en, clk, clr
  Multiplexer multiplexer_7 (.in0(reg_1_p7), .in1(reg_1_p1[0]), .out(multiplexer_7_out[0]), .sel(BFrwd2));
  Register #(.width(32)) Imm (.D(immediate_1_imm), .Q(Imm_q));  // open: en, clk, clr
  Register #(.width(32)) Inst_XM (.D(multiplexer_5_out), .Q(Inst_XM_q));  // open: en, clk, clr
  Register #(.width(32)) br_pred_taken_xm (.D(br_pred_taken), .Q(br_pred_taken_xm_q));  // open: en, clk, clr
  Multiplexer #(.width(32)) multiplexer_8 (.in0(A_q), .in1(reg_1_p1), .out(multiplexer_8_out), .sel(AFrwd1));
  Multiplexer #(.width(32)) multiplexer_9 (.in0(B_q), .in1(reg_1_p1), .out(store_1_p2), .sel(BFrwd1));
  Multiplexer multiplexer_10 (.in0(Inst_XM_q[0]), .in1(NOP_FLUSHING), .out(multiplexer_10_out[0]), .sel(flush_w_q[0]));
  Adder #(.width(14)) adder_4 (.a(14'h4), .b(PC_XM_q[13:0]), .out(adder_4_out));  // open: cin, cout
  Multiplexer #(.width(32)) multiplexer_11 (
    .in0(multiplexer_8_out), .in1(PC_XM_q), .out(multiplexer_11_out), .sel(ASel));
  Multiplexer #(.width(32)) multiplexer_12 (.in0(store_1_p2), .in1(Imm_q), .out(multiplexer_12_out), .sel(BSel));
  Branch branch_1 (.A(multiplexer_8_out), .B(store_1_p2), .BrSel(BrSel), .BrTaken(BrTaken));
  Forwarding forwarding_1 (.Inst_XM(multiplexer_10_out[0]));  // open: Inst_FD, Inst_W, AFrwd1, BFrwd1, AFrwd2, BFrwd2, JalrFrwd
  // XM_logic xm_logic_1: pin names not known; wires that end beside it: multiplexer_10_out, br_pred_taken_xm_q, xm_logic_1_p3
  Register #(.width(32)) flush_w (.D(xm_logic_1_p3), .Q(flush_w_q));  // open: en, clk, clr
  ALU alu_1 (.A(multiplexer_11_out), .B(multiplexer_12_out), .ALUSel(ALUSel), .result(store_1_p1));
  // store store_2: pin names not known; wires that end beside it: store_1_p1, store_1_p2, MemRW, store_2_p4, store_2_p5, store_2_p6
  Register PC_W (.D(PC_XM_q[7:0]), .Q(PC_W_q[7:0]));  // open: en, clk, clr
  Register #(.width(32)) ALU_RESULT_W (.D(store_1_p1), .Q(ALU_RESULT_W_q));  // open: en, clk, clr
  Register #(.width(32)) Inst_W (
    .D(multiplexer_10_out), .Q({Inst_W_q[31:12], reg_1_p2, Inst_W_q[6:0]}));  // open: en, clk, clr
  // DMEM dmem_1: pin names not known; wires that end beside it: store_2_p4, store_2_p5, store_2_p6, dmem_1_p4
  // UART_read uart_read_1: pin names not known; wires that end beside it: ready_to_receive, uart_read_1_p2, uart_write_1_p3[1]
  // UART_write uart_write_1: pin names not known; wires that end beside it: store_1_p2, write_valid, uart_write_1_p3[0]
  Register total_branch_counter (.D(adder_6_out[7:0]), .Q(total_branch_counter_q[7:0]));  // open: en, clk, clr
  Adder #(.width(14)) adder_5 (.a(14'h4), .b(PC_W_q), .out(adder_5_out));  // open: cin, cout
  W_logic w_logic_1 (.br_pred_taken(br_pred_taken[0]));  // open: InstW, InstFd, BIOSRest, PCSel, RegWEn, CSRWen, WBSel
  Register cycle_counter (.D(adder_7_out[7:0]), .Q(cycle_counter_q[7:0]));  // open: en, clk, clr
  Register Inst_counter (.D(adder_8_out[7:0]), .Q(Inst_counter_q[7:0]));  // open: en, clk, clr
  Adder #(.width(14)) adder_6 (.a(is_branch_instr), .b(total_branch_counter_q), .out(adder_6_out));  // open: cin, cout
  // load load_1: pin names not known; wires that end beside it: ALU_RESULT_W_q, dmem_1_p4, load_1_p3
  // load load_2: pin names not known; wires that end beside it: ALU_RESULT_W_q, bios_1_p4, load_2_p3
  Register correct_branch_counter (.D(adder_9_out[7:0]), .Q(correct_branch_counter_q[7:0]));  // open: en, clk, clr
  Adder #(.width(14)) adder_7 (.a(14'h1), .b(cycle_counter_q), .out(adder_7_out));  // open: cin, cout
  Adder #(.width(14)) adder_8 (
    .a({undriven_2, NotFlushSEL}), .b(Inst_counter_q), .out(adder_8_out));  // open: cin, cout
  Multiplexer #(.select(4)) multiplexer_13 (
    .in4(load_1_p3), .in5(ALU_RESULT_W_q[0]), .in6(adder_5_out[0]), .in7(uart_read_1_p2),
    .in8(uart_write_1_p3[0]), .in9(cycle_counter_q[0]), .in10(Inst_counter_q[0]), .in11(load_2_p3),
    .in12(total_branch_counter_q[0]), .in13(correct_branch_counter_q[0]), .out(reg_1_p1[0]), .sel(WBSel));  // open: in0, in1, in2, in3, in14, in15
  Adder #(.width(14)) adder_9 (
    .a(is_prediction_correct), .b(correct_branch_counter_q), .out(adder_9_out));  // open: cin, cout
  // Pins of 1 and 32 bits meet at ImmSel
  // Pins of 1 and 32 bits meet at br_pred_taken
  // Pins of 1 and 14 bits meet at is_branch_instr
  // Pins of 1 and 32 bits meet at {{30{1'b0}}, uart_write_1_p3}
  // Pins of 1 and 14 bits meet at {undriven_2, NotFlushSEL}
  // Pins of 1 and 4 bits meet at WBSel
  // Pins of 1 and 14 bits meet at is_prediction_correct
  // Pins of 1 and 32 bits meet at reg_1_p1
  // Pins of 1 and 8 bits meet at multiplexer_6_out
  // Pins of 1 and 32 bits meet at multiplexer_7_out
  // Pins of 1 and 32 bits meet at Inst_XM_q
  // Pins of 1 and 32 bits meet at multiplexer_10_out

  // Other names for the same wires on the sheet: IMemWE = PC_XM_30; InstSel = PC_FD_30

  // Notes on the sheet:
  //   a
  //   jal & branch predict taken
  //   alu_result
  //   pc+4
  //   alu
  //   alu_w
  //   jalr
  //   alu_xm
  //   IF CSRW || CSRWI
  //   fd/xm/w
  //   fd/xm/w
endmodule

module IMEM (
  input  A_wbe,
  input  A_din,
  input  A_addr,
  input  B_addr,
  input  clk,
  output [31:0] B_dout
);
endmodule

module Reg (
  input  DataD,
  input  AddrD,
  input  AddrA,
  input  AddrB,
  input  clk,
  input  RegWE,
  output [31:0] DataA,
  output [31:0] DataB
);
endmodule

module DMEM (
  input  [31:0] din,
  input  wbe,
  input  [13:0] addr,
  input  clk,
  output [31:0] dout
);
endmodule

module ALU (
  input  [31:0] A,
  input  [31:0] B,
  input  ALUSel,
  output [31:0] result
);
endmodule

module Branch (
  input  [31:0] A,
  input  [31:0] B,
  input  BrSel,
  output BrTaken
);
endmodule

module immediate (
  input  [31:0] Instruc,
  input  [31:0] ImmSel,
  output [31:0] Imm
);
endmodule

module Forwarding (
  input  Inst_FD,
  input  Inst_XM,
  input  Inst_W,
  output AFrwd1,
  output BFrwd1,
  output AFrwd2,
  output BFrwd2,
  output JalrFrwd
);
endmodule

module FD_logic (
  input  InstFd,
  input  PCFd,
  output InstSel,
  output ImmSell
);
endmodule

module BIOS (
  input  A_addr,
  input  A_en,
  input  B_addr,
  input  B_en,
  input  clk,
  output [31:0] A_dout,
  output [31:0] B_dout
);
endmodule

module UART_read (
  input  ready_recieve,
  output [13:0] read,
  output [31:0] read_valid
);
endmodule

module UART_write (
  input  [13:0] write,
  input  [31:0] write_valid,
  output ready_to_write
);
endmodule

module load (
  input  addr,
  input  data_in,
  input  func3,
  input  opcode,
  output load_data
);
endmodule

module store (
  input  addr,
  input  din,
  input  func3_xm,
  input  we,
  output store_data,
  output MemRW4,
  output mem_addr
);
endmodule

module XM_logic (
  input  InstXm,
  input  BrTaken,
  input  br_pred_taken_xm,
  output BrSel,
  output ASel,
  output BSel,
  output MemRW,
  output IMemWE,
  output ALUSel,
  output UART_write_valid,
  output UART_ready_to_receive,
  output Flush,
  output DoNotBranch
);
endmodule

module W_logic (
  input  InstW,
  input  InstFd,
  input  BIOSRest,
  input  br_pred_taken,
  output PCSel,
  output RegWEn,
  output CSRWen,
  output WBSel
);
endmodule

module Branch_Pred_logic (
  input  PC_FD,
  input  is_branch_fd,
  input  PC_XM,
  input  is_branch_xm,
  input  br_result,
  output br_pred_taken
);
endmodule
