// Logisim project cpu.circ as structural Verilog: 10 circuits, main circuit main
module main (
  input  PC30
);

  wire dmem_1_p3;
  wire [7:0] reg_1_p5;
  wire [13:0] adder_1_out, adder_2_out, alu_1_p3, multiplexer_1_out, PC_q;
  wire [31:0] A_q, B_q, bios_1_p2, imem_1_p2, Imm_q, immediate_1_imm, Inst_XM_q, multiplexer_2_out,
       multiplexer_3_out, multiplexer_4_out, multiplexer_5_out, PC_XM_q, reg_1_p1, reg_1_p2, reg_1_p6;

  Register #(.width(14)) PC (.D(multiplexer_1_out), .Q(PC_q));  // open: en, clk, clr
  Multiplexer #(.width(14)) multiplexer_1 (.in0(adder_1_out), .in1(alu_1_p3), .out(multiplexer_1_out));  // open: sel
  Adder #(.width(14)) adder_1 (.a(14'h3ffc), .b(PC_q), .out(adder_1_out));  // open: cin, cout
  Controls controls_1 ();  // open: BrEq, BrLT, Inst_FD, Inst_XM, Inst_W, PCSel, RegWEn, ImmSel, BrUn, Bsel, ASel, ALUSel, MemRW, WBSel
  // IMEM imem_1: pin names not known; wires that end beside it: PC_q, imem_1_p2
  // BIOS bios_1: pin names not known; wires that end beside it: PC_q, bios_1_p2
  Multiplexer #(.width(32)) multiplexer_2 (.in0(imem_1_p2), .in1(bios_1_p2), .out(multiplexer_2_out), .sel(PC30));
  // Reg reg_1: pin names not known; wires that end beside it: reg_1_p1, reg_1_p2, multiplexer_2_out[19:15], multiplexer_2_out[31:20], reg_1_p5, reg_1_p6
  immediate immediate_1 (.Instruc(multiplexer_2_out), .Imm(immediate_1_imm));
  Register PC_XM (.D(PC_q[7:0]), .Q(PC_XM_q[7:0]));  // open: en, clk, clr
  Register A (.D(reg_1_p5), .Q(A_q[7:0]));  // open: en, clk, clr
  Register #(.width(32)) B (.D(reg_1_p6), .Q(B_q));  // open: en, clk, clr
  Register #(.width(32)) Imm (.D(immediate_1_imm), .Q(Imm_q));  // open: en, clk, clr
  Register #(.width(32)) Inst_XM (.D(multiplexer_2_out), .Q(Inst_XM_q));  // open: en, clk, clr
  Branch branch_1 (.A(A_q), .B(B_q));  // open: BrUn, BrEq, BrLT
  Multiplexer #(.width(32)) multiplexer_3 (.in0(A_q), .in1(PC_XM_q), .out(multiplexer_3_out));  // open: sel
  Multiplexer #(.width(32)) multiplexer_4 (.in0(B_q), .in1(Imm_q), .out(multiplexer_4_out));  // open: sel
  // ALU alu_1: pin names not known; wires that end beside it: multiplexer_3_out, multiplexer_4_out, alu_1_p3
  Adder #(.width(14)) adder_2 (.a(14'h3ffc), .b(PC_XM_q[13:0]), .out(adder_2_out));  // open: cin, cout
  // DMEM dmem_1: pin names not known; wires that end beside it: alu_1_p3, B_q, dmem_1_p3
  Register #(.width(32)) DATA (.D(multiplexer_5_out), .Q(reg_1_p1));  // open: en, clk, clr
  Multiplexer #(.select(2)) multiplexer_5 (
    .in0(dmem_1_p3), .in1(alu_1_p3[0]), .in2(adder_2_out[0]), .out(multiplexer_5_out[0]));  // open: in3, sel
  Register #(.width(32)) Inst_M (.D(Inst_XM_q), .Q(reg_1_p2));  // open: en, clk, clr
  // Pins of 8 and 32 bits meet at A_q
  // Pins of 8 and 14 and 32 bits meet at PC_XM_q
  // Pins of 1 and 14 bits meet at alu_1_p3
  // Pins of 1 and 14 bits meet at adder_2_out
  // Pins of 1 and 32 bits meet at multiplexer_5_out
  // Pins of 8 and 14 bits meet at PC_q
endmodule

module IMEM (
  input  A_din,
  input  A_addr,
  input  A_wbe,
  input  B_din,
  input  B_addr,
  input  B_wbe,
  input  clk,
  output [31:0] A_dout,
  output [31:0] B_dout
);
endmodule

module Reg (
  input  DataD,
  input  AddrD,
  input  AddrA,
  input  AddrB,
  input  clk,
  output [31:0] DataA,
  output [31:0] DataB
);
endmodule

module DMEM (
  input  [13:0] addr,
  input  [31:0] din,
  input  wbe,
  input  clk,
  output [31:0] dout
);
endmodule

module ALU (
  input  [31:0] A,
  input  [31:0] B,
  input  ALUSel,
  output [31:0] result
);
endmodule

module Branch (
  input  [31:0] A,
  input  [31:0] B,
  input  BrUn,
  output BrEq,
  output BrLT
);
endmodule

module immediate (
  input  [31:0] Instruc,
  output [31:0] Imm
);
endmodule

module Forwarding (
  input  Inst_FD,
  input  Inst_XM,
  input  Inst_W
);
endmodule

module Controls (
  input  BrEq,
  input  BrLT,
  input  Inst_FD,
  input  Inst_XM,
  input  Inst_W,
  output PCSel,
  output RegWEn,
  output ImmSel,
  output BrUn,
  output Bsel,
  output ASel,
  output ALUSel,
  output MemRW,
  output WBSel
);
endmodule

module BIOS (
  input  A_din,
  input  A_addr,
  input  A_wbe,
  input  B_din,
  input  B_addr,
  input  B_wbe,
  input  clk,
  output [31:0] A_dout,
  output [31:0] B_dout
);
endmodule
